# Fritzing sketch ControladoraTermicaProgramable-V 00 (saved by Fritzing 0.9.7b)
circuit board: 5.93289cm x 6.83857cm
circuit board: 15.7268cm x 13.8598cm
circuit board: 8.17126cm x 5.90426cm
circuit board: 5.8818cm x 5.91898cm
circuit board: 7.53063cm x 2.97169cm
circuit board: 3.94407cm x 1.47231cm
circuit board: 8.17126cm x 5.90426cm
circuit board: 3.67256cm x 2.50225cm

parts:
  J1 = Piezo Speaker
  LED1 = LED - 5mm [color="Red (633nm)" current=0.030 package="5 mm [THT]"]
  LED2 = LED - 5mm [color="Green (570nm)" current=0.030 package="5 mm [THT]"]
  LED3 = LED - 5mm [color="Red (660nm)" current=0.030 package="5 mm [THT]"]
  LED4 = LED - 5mm [color="Blue (505nm)" current=0.030 package="5 mm [THT]"]
  DS1 = DS18B20 1-Wire Temperature Sensor [part_number=DS18B20]
  U3 = mystery part, 5 pins [chip_label="FUENTE ATX"]
  J2 = Peltier Element
  Q2 = NPN-Transistor [package="TO92 [THT]"]
  R3 = Resistor [tolerance=±5% power=0.25 resistance=4.7k package=THT]
  R5 = Resistor [tolerance=±5% power=0.25 resistance=220 package=THT]
  LED5 = LED - 5mm [color="Blue (470nm)" current=0.030 package="5 mm [THT]"]
  Q3 = Basic FET P-Channel [part_number="IRF 4905" package="TO220 [THT]"]
  Q4 = Basic FET P-Channel [part_number="IRF 4905" package="TO220 [THT]"]
  Q6 = Basic FET N-Channel [part_number="IRF Z44N" package="TO220 [THT]"]
  Q5 = Basic FET N-Channel [part_number="IRF Z44N" package="TO220 [THT]"]
  J3 = Screw terminal - 2 pins [package=THT]
  Q7 = NPN-Transistor [package="TO92 [THT]"]
  Q8 = NPN-Transistor [package="TO92 [THT]"]
  IC1 = IC, DIP package, 8 pins [chip_label=IC]
  L1 = Inductor [package="400 mil [THT]"]
  R7 = Resistor [tolerance=±5% power=0.25 resistance=47k package=THT]
  R8 = Resistor [tolerance=±5% power=0.25 resistance=180 package=THT]
  D1 = Schottky Diode [part_number=1N5817 package="300 mil [THT]"]
  R10 = Resistor [tolerance=±5% power=0.25 resistance=220 package=THT]
  R11 = Resistor [tolerance=±5% power=0.25 resistance=10k package=THT]
  R12 = Resistor [tolerance=±5% power=0.25 resistance=10k package=THT]
  R13 = Resistor [tolerance=±5% power=0.25 resistance=220 package=THT]
  D2 = Rectifier Diode [part_number=1N4001 package="300 mil [THT]"]
  D3 = Rectifier Diode [part_number=1N4001 package="300 mil [THT]"]
  D4 = Rectifier Diode [part_number=1N4001 package="300 mil [THT]"]
  D5 = Rectifier Diode [part_number=1N4001 package="300 mil [THT]"]
  R14 = Resistor [tolerance=±5% power=0.25 resistance=0.22 package=THT]
  R15 = Resistor [tolerance=±5% power=0.25 resistance=220 package=THT]
  R16 = Resistor [tolerance=±5% power=0.25 resistance=220 package=THT]
  R17 = Resistor [tolerance=±5% power=0.25 resistance=2.2k package=THT]
  ZS-042_RTC1 = ZS-042 RTC Module
  C7 = Ceramic Capacitor [capacitance=0.15nF voltage=35V package="100 mil [THT, multilayer]"]
  C5 = Ceramic Capacitor [capacitance=100nF voltage=35V package="200 mil [THT, multilayer]"]
  C4 = Electrolytic Capacitor [capacitance=470µF voltage=35V package="300 mil [THT, electrolytic]"]
  Q1 = Basic FET N-Channel [part_number="IRF Z44N" package="TO220 [THT]"]
  R18 = Resistor [tolerance=±5% power=0.25 resistance=2.2k package=THT]
  U4 = Optocoupler [package=THT]
  R19 = Resistor [tolerance=±5% power=0.25 resistance=220 package=THT]
  C8 = Electrolytic Capacitor [capacitance=1µF voltage=35V package="100 mil [THT, electrolytic]"]
  J7 = Screw terminal - 2 pins [package=THT]
  R21 = Resistor [tolerance=±5% power=0.25 resistance=220 package=THT]
  J8 = screw terminal, 3 pins
  R22 = Resistor [tolerance=±5% power=0.25 resistance=220 package=THT]
  LED6 = LED - 5mm [color="Blue (505nm)" current=0.030 package="5 mm [THT]"]
  LED7 = LED - 5mm [color="Blue (505nm)" current=0.030 package="5 mm [THT]"]
  R24 = Resistor [tolerance=±5% power=0.25 resistance=220 package=THT]
  LED8 = LED - 5mm [color="Blue (505nm)" current=0.030 package="5 mm [THT]"]
  J10 = screw terminal, 8 pins
  J11 = screw terminal, 4 pins
  M1 = DC Motor
  R25 = Resistor [tolerance=±5% power=0.25 resistance=220 package=THT]
  Componente1 = Arduino Uno (Rev3)
  R20 = Resistor [tolerance=±5% power=0.25 resistance=220 package=THT]
  J12 = screw terminal, 10 pins
  J13 = screw terminal, 10 pins
  J14 = Screw terminal - 2 pins [package=THT]
  J15 = Screw terminal - 2 pins [package=THT]
  Pad1 = Pad [width=2 height=3 connect=center]  # not connected

nets:
  N1: J1.pin1, Q2.C
  VDD: J1.pin2, DS1.VDD, R3.Pin_0, ZS-042_RTC1.VCC, C8.+, R21.Pin_0, J8.pin1, Componente1.5V
  N2: LED1.cathode, LED2.cathode, J2.pin2, Q4.source, Q5.drain, J3.pin2, D2.anode, D3.cathode
  N3: LED1.anode, LED2.anode, J2.pin1, Q3.source, Q6.drain, J3.pin1, D4.anode, D5.cathode
  GND: LED3.cathode, LED4.cathode, DS1.GND, U3.pin1, Q2.E, Q6.source, Q5.source, Q7.E, Q8.E, IC1.pin2, IC1.pin4, D3.anode, D5.anode, R17.Pin_1, ZS-042_RTC1.GND, C7.1, C5.0, C4.-, Q1.source, U4.Pin_2, U4.Pin_4, C8.-, J7.pin2, J8.pin3, LED6.cathode, LED7.cathode, LED8.cathode, J10.pin8, J11.pin3, M1.pin_1, Componente1.GND, J12.pin3, J12.pin5, J12.pin7, J13.pin3, J13.pin5, J13.pin6, J13.pin7, J14.pin2
  N4: LED3.anode, R19.Pin_1, J10.pin2
  N5: LED4.anode, J10.pin1, R20.Pin_1
  N6: DS1.DQ, R3.Pin_1, J8.pin2, Componente1.D4
  N7: U3.pin2, LED5.anode, Q3.drain, Q4.drain, IC1.pin6, D2.cathode, D4.cathode, R14.Pin_1, C5.1, R19.Pin_0, J7.pin1, J11.pin1, J11.pin4, M1.pin_2, J12.pin10, J15.pin1
  N8: U3.pin3, U4.Pin_5, J13.pin4
  N9: U3.pin4, R21.Pin_1, J12.pin9
  N10: U3.pin5, J13.pin9, J13.pin10, J14.pin1
  N11: Q2.B, R5.Pin_0
  N12: R5.Pin_1, Componente1.A0
  N13: LED5.cathode, Q1.drain, J11.pin2
  N14: Q3.gate, R12.Pin_1, R13.Pin_0
  N15: Q4.gate, R10.Pin_0, R11.Pin_1
  N16: Q6.gate, Q7.C, R13.Pin_1
  N17: Q5.gate, Q8.C, R10.Pin_1
  N18: Q7.B, R15.Pin_1
  N19: Q8.B, R16.Pin_1
  N20: IC1.pin1, L1.pin_0, D1.anode
  N21: IC1.pin3, C7.0
  N22: IC1.pin5, R7.Pin_0, R17.Pin_0
  N23: IC1.pin7, L1.pin_1, R8.Pin_0, R14.Pin_0
  N24: IC1.pin8, R8.Pin_1
  N25: R7.Pin_1, D1.cathode, R11.Pin_0, R12.Pin_0, C4.+
  N26: R15.Pin_0, Componente1.D5_PWM
  N27: R16.Pin_0, Componente1.D6_PWM
  N28: ZS-042_RTC1.SDA, Componente1.A4/SDA
  N29: ZS-042_RTC1.SCL, Componente1.A5/SCL
  N30: Q1.gate, R18.Pin_1
  N31: R18.Pin_0, Componente1.D11_PWM/MOSI
  N32: U4.Pin_1, Componente1.D9_PWM
  N33: R22.Pin_0, Componente1.D10_PWM/SS
  N34: R22.Pin_1, LED6.anode, J10.pin5
  N35: LED7.anode, J10.pin4, R25.Pin_1
  N36: R24.Pin_0, Componente1.D12/MISO
  N37: R24.Pin_1, LED8.anode, J10.pin6
  N38: R25.Pin_0, Componente1.D7
  N39: Componente1.D13/SCK, R20.Pin_0

notes:
  PLACA PELTIER
  RTC CLOCK +ram
  LED
  FOTOPERIODO
  MICRO-P
  ARDU-UNO
  BUZZER PASIVO
  PUENTE-H SIMPLE / DISCRETO
  CON:
  4 MOSFET= IRF Z44N IRF 4905 + UPPER CI= MC -34063 A
  FUENTE ATX
  1GND BLACK
  2VDD 12V 10A YELLOW
  3PWR-ON GREEN
  4 STANBY 5v10A VIOLET
  5 DC 5v 25A RED
  SENSOR- TEMP
  DS18 B 20
  version entubada
  3- Rojo (+VCC), +5v
  2-amarillo(DATA),i2C
  1-Negro (GND)
  Pull-Up 4.7k Ohm entre pins 2y 3
  2-(DQ=Data In/Out) y 3-(Vdd)
  FRIO
  CALOR
  Fan 12v FOTOPERIODO tira led 12v
  +12 gnd Led +12
  UPPER CI:
  MC -34063 A
  +19/28v
  +12 GND
  PWM
  +12v
  GND
  PWM a PWM b
  +19v
  MC-34063
  PUENTE-H CON 4 MOSFET SIMPLE / DISCRETO
  RTC=
  DS3231 + EEPROM AT24C32
  COM I2C
  ATX
  1GND NEGRO
  2VDD 12V YELLOW
  3PWR-ON VERDE
  4 STANBY 5v VIOLET
  5 DC 5v RED
  REPOSITORIO: Eduarq NUBE e01kreiman@gmail.com
  https://docs.google.com/document/d/1vcTVYxaLnhMcUdjbMWwd1TrjF9DZqiPkKovk91h1lXA/edit?usp=share_link
  coneciones:
  ONE_WIRE_BUS 12
  // 0X3C+SA0 - 0x3C or 0x3D
  #define I2C_ADDRESS 0x3C
  const int BUZZER = A0; //buzzer con led azul en paralelo usa pasivo con trNPN buffer rutina de tono 450Hz libreria easyBuzzer
  // protocolo de comunicacion I2C Arduino UNO, NANO reserva por default -> SDA = A4 y SCL = A5 NANO
  //#define SCL 5 protocolo de comunicacion I2C The compiler will replace any mention of scl with the value 5 at compile time.
  //#define SDA 4 protocolo de comunicacion I2C The compiler will replace any mention of scl with the value 4 at compile time.
  #define pinFOTOPERIODO 11
  int inApin[2] = { 7, 4 }; // INA: Clockwise input sentido horario FRIO
  int inBpin[2] = { 8, 9 }; // INB: Counter-clockwise input sentido anti-horario CALOR
  int pwmpin[2] = { 5, 6 }; // PWM input
  const int pinOPTOCUPLER = 9; // Led OPTOCUPLER cable verde de fuente
  const int pinPOTE = A3; // pote usar pin analog read MONITOREAR TENSION PUENTE H
  // PULSADORES SELECTORES
  pinMode(Sw3, INPUT); // pin ardu A1 pull down con resistencia 1K5 y FILTRO 100NF en PCB
  pinMode(Sw2, INPUT); // pin ardu A2 pull down con resistencia 1K5 y FILTRO 100NF en PCB
  pinMode(pinOPTOCUPLER, OUTPUT);
  pinMode(BUZZER, OUTPUT);
  pinMode(pinFOTOPERIODO, OUTPUT);
  EasyBuzzer.setPin(14);
  Led FUENTE ON
  Led ECO d13
  ON fuente
  eco 13
  PELTIER
  IRF Z44N 4N35
  coneciones:
  ONE_WIRE_BUS 12
  // 0X3C+SA0 - 0x3C or 0x3D
  #define I2C_ADDRESS 0x3C
  const int pinEVENTO = A0; // BOTON EVENTO
  const int pinSTART = A1; // BOTON START/INICIO
  const int pinABORT = A2; // BOTON ABORT/Stop
  const int pinPOTE = A3; // pote usar pin analog read MONITOREAR TENSION PUENTE H
  const int pinCirca = 10; //pwm desde zocalo SD led frontal ROJO
  const int pinTCrict = 11; //pwm desde zocalo SD led frontal YELLOW
  const int pinAlone = 12; // desde zocalo SD led frontal YELLOW
  // protocolo de comunicacion I2C Arduino UNO, NANO reserva por default -> SDA = A4 y SCL = A5 NANO
  //#define SCL 5 protocolo de comunicacion I2C The compiler will replace any mention of scl with the value 5 at compile time.
  //#define SDA 4 protocolo de comunicacion I2C
  //--DEFINE Arduino pines DIGITALES
  // PUERTO SERIAL 0
  // PUERTO SERIAL 1
  const int BUZZER = 2; //D2 reservalo para usar hard interrupt
  //pin digital D3 //D3 reservalo para usar hard interrupt
  // pinDatosDQ 4 // Pin del Sensor Peltier donde se conecta el bus OneWire -------> pin digital D4
  const int pinINVERSOR_A = 5; //Dp05 pinA Puente H USAR PINES – 5 y 6 cuando usa LIBRERIA TIMERONE Timer0
  const int pinINVERSOR_B = 6; //Dp06 pinB Puente H
  // 7 LIBRE
  // 8 LIBRE
  const int pinOPTOCUPLER = 9; // Led OPTOCUPLER cable verde de fuente
  // 10 LIBRE desde zocalo SD
  // 11 control LED fotoperiodo
  // 12 LIBRE desde zocalo SD
  const int LedPin = 13; //onboard PCB y led AZUL frontal, tambien usado por comunicacion
  Led Circa 10
  Led TCrict 7
  Led Alone 12
  sensor temp
  DS1820
  Fan 12v
  Alone 12
  Circa 10
  TCrict 07
  07
  10
  12
  13
  conector fuente ATX 24 Hembra a PCB lado soldadura
  hembra lado soldadura
  3.3 naranja
  -12 azul
  gnd negro
  p ON green
  gnd negro
  gnd negro
  gnd negro
  -5v blanco
  +5 rojo
  +5 rojo
  hembra lado soldadura
  3v3 naranja
  3v3 naranja
  gnd negro
  +5 rojo
  gnd negro
  +5 rojo
  gnd negro
  PG gris
  +5 StBy violeta
  +12v amarillo
  +5 rojo
  gnd negro
  +12v amarillo
  +3.3 naranja
  CONECTOR
  hembra ATX
  lado soldadura
