# Fritzing sketch ControladoraTermicaProgramable-V2  IC-PH (saved by Fritzing 0.9.7b)
circuit board: 5.21207cm x 5.29151cm
circuit board: 14.9537cm x 13.5012cm

parts:
  Componente1 = Arduino Uno (Rev3)
  S1 = Pushbutton [package="[THT]"]
  S2 = Pushbutton [package="[THT]"]
  J1 = Piezo Speaker
  LED1 = LED - 5mm [color="Red (633nm)" current=0.030 package="5 mm [THT]"]
  LED2 = LED - 5mm [color="Green (570nm)" current=0.030 package="5 mm [THT]"]
  LED3 = LED - 5mm [color="Red (660nm)" current=0.030 package="5 mm [THT]"]
  LED4 = LED - 5mm [color="Blue (505nm)" current=0.030 package="5 mm [THT]"]
  DS1 = DS18B20 1-Wire Temperature Sensor [part_number=DS18B20]
  OLED2 = OLED 128x64 I2C Monochrome Display
  U3 = mystery part, 5 pins [chip_label="FUENTE ATX"]
  J2 = Peltier Element
  Q2 = NPN-Transistor [package="TO92 [THT]"]
  C1 = Ceramic Capacitor [capacitance=100nF voltage=35V package="100 mil [THT, multilayer]"]
  C2 = Ceramic Capacitor [capacitance=100nF voltage=35V package="100 mil [THT, multilayer]"]
  R1 = Resistor [tolerance=±5% power=0.25 resistance=220 package=THT]
  R2 = Resistor [tolerance=±5% power=0.25 resistance=220 package=THT]
  R3 = Resistor [tolerance=±5% power=0.25 resistance=220 package=THT]
  RE2 = KY-040 Rotary encoder [part_number="rotary Coder" package=THT]
  R5 = Resistor [tolerance=±5% power=0.25 resistance=220 package=THT]
  LED5 = LED - 5mm [color="Blue (470nm)" current=0.030 package="5 mm [THT]"]
  ZS-042_RTC1 = ZS-042 RTC Module
  Q1 = Basic FET N-Channel [package="TO220 [THT]"]
  R18 = Resistor [tolerance=±5% power=0.25 resistance=2.2k package=THT]
  U4 = Optocoupler [package=THT]
  R19 = Resistor [tolerance=±5% power=0.25 resistance=220 package=THT]
  R20 = Resistor [tolerance=±5% power=0.25 resistance=220 package=THT]
  U6 = mystery part, 6 pins [chip_label="PUENTE H DOBLE ANAGOG A0-A5"]  # not connected
  U8 = mystery part, 8 pins [chip_label="RX TX  PUENTE H DOBLE"]
  J4 = Screw terminal - 2 pins [package=THT]
  J5 = Screw terminal - 2 pins [package=THT]  # not connected
  J6 = Screw terminal - 2 pins [package=THT]
  U5 = mystery part, 10 pins [chip_label="PUENTE H DOBLE D13 a D8"]
  U7 = mystery part, 8 pins [chip_label="PUENTE H DOBLE RESET VIN"]

nets:
  N1: Componente1.A0, R5.Pin_1
  N2: Componente1.A1, S1.Pin_3, S1.Pin_4, C2.1, R2.Pin_1
  N3: Componente1.A2, S2.Pin_3, S2.Pin_4, C1.1, R1.Pin_1
  N4: Componente1.A4/SDA, OLED2.SDA, ZS-042_RTC1.SDA
  N5: Componente1.A5/SCL, OLED2.SCK, ZS-042_RTC1.SCL
  N6: Componente1.D8, U5.pin1
  N7: Componente1.D9_PWM, U4.Pin_1
  N8: Componente1.D11_PWM/MOSI, R18.Pin_0
  N9: Componente1.D12/MISO, DS1.DQ, R3.Pin_1
  GND: Componente1.GND, LED3.cathode, LED4.cathode, DS1.GND, OLED2.GND, U3.pin1, Q2.E, C1.0, C2.0, R1.Pin_0, R2.Pin_0, RE2.GND, ZS-042_RTC1.GND, Q1.source, U4.Pin_2, U4.Pin_4, J4.pin1, U7.pin2, U7.pin3
  N10: Componente1.D2, RE2.CLK
  N11: Componente1.D3_PWM, RE2.DT
  N12: Componente1.D4, RE2.SW
  N13: Componente1.D5_PWM, U8.pin6
  N14: Componente1.D7, U8.pin8
  VDD: Componente1.5V, S1.Pin_1, S1.Pin_2, S2.Pin_1, S2.Pin_2, J1.pin2, DS1.VDD, OLED2.VDD, R3.Pin_0, RE2.Vcc, ZS-042_RTC1.VCC
  N15: J1.pin1, Q2.C
  N16: LED1.cathode, LED2.cathode, J2.pin2, J6.pin1
  N17: LED1.anode, LED2.anode, J2.pin1, J6.pin2
  N18: LED3.anode, R19.Pin_1
  N19: LED4.anode, R20.Pin_1
  N20: U3.pin2, LED5.anode, R19.Pin_0, J4.pin2
  N21: U3.pin3, U4.Pin_5
  N22: U3.pin5, U7.pin4
  N23: Q2.B, R5.Pin_0
  N24: LED5.cathode, Q1.drain
  N25: Q1.gate, R18.Pin_1

notes:
  PLACA PELTIER
  RTC CLOCK
  MEMORIA
  RTC
  LED
  FOTOPERIODO
  PUENTE-H
  VNH 3ASP30
  DOBLE
  STEPPER
  ROTATIVO
  DISPLAY OLED I2C
  SSD1306
  SWITCH
  HUYE
  FUENTE 12vDC
  ATX
  SWITCH
  ACEPTA
  SWITCH
  CAMBIA
  MICRO-P
  ARDU-UNO
  BUZZER PASIVO
  PUENTE-H 1
  3IN B a D7
  4IN B a D8
  5 PWM a D5
  enable 2 A1
  ATX
  1GND NEGRO
  2VDD 12V YELLOW
  3PWR-ON VERDE
  4 STANBY 5v VIOLET
  5 DC 5v RED
  SENSOR- TEMP
  DS18 B 20
  FRIO
  CALOR
  FOTOPERIODO
  IRF
  RTC=
  DS3231 + EEPROM AT24C32
  COM I2C
  display
  OLED
  --Manual de uso --------------------------------------------------------------------------------
  Operadores:
  A boton: ciclico para entrar y salir del menu en curso
  B boton pulso corto avanza decimas de grado o 5 minutos de hora
  B boton pulso mayor de 10 Sg ciclico para pasar de T1 a T2 o de Dia a Noche
  C pulsad rotativo Amarillo -OK/ACEPTA-acepta la opcion o el campo mostrado en el display
  Entra y Sale ->A
  Cambia Numeros ->Rotor
  Acepta ->C=OK
  Cambia decimales ->B pulso 1 Sg
  Cambia Campos ->B mayor de 10 Sg ciclico
  --------------------------------------------------------------------------------------------------
  Menues o pantallas:
  0- inicial y constante:
  pulsando A se pasa al siguiente menu y siempre se vuelve a esta pantalla/Menu.
  muestra las temperaturas Min=T1 y Max=T2 y el Modo o Programa termico.
  muestra la temperatura instantanea del sensor del interior de la Camara.
  muestra la temperatura Goal a lograr en ese instante.
  muestra la diferencia en Grados entre ambas.
  la hora actual, el minuto de disparo del autoreset.
  1- menu Seteador : selecciona el ingreso a los siguientes menues:
  2- menu Modo/Progs: selecciona Programas de comportamiento termico:
  temp costante (Termostato)
  temp Lineal (y=mx+b)
  circadiano (modelo Parton/Logan)
  3- menu Temp : parametriza T1 y T2 ( Temperaturas Minima y Maxima a desarrollar en el tiempo)
  4- menu Foto : simula el fotoperiod regulando la iluminacion del interior de la camara
  parametriza amanecer y anochecer (fotoperiodo) ( Dia y Noche)
  --------------------------------------------------------------------------------------
  Tiempo pulso
  corto
  largo pasa de hora a minuto toggle circular
  A B pulso corto
  - -
  + - corto aumenta hora/min/temp
  - + corto decrece hora/min/temp
  + - largo llama menu circular
  + +
  C pulsad OK/ACEPTA
  coneciones:
  ONE_WIRE_BUS 12
  // 0X3C+SA0 - 0x3C or 0x3D
  #define I2C_ADDRESS 0x3C
  const int BUZZER = A0; //buzzer con led azul en paralelo usa pasivo con trNPN buffer rutina de tono 450Hz libreria easyBuzzer
  // protocolo de comunicacion I2C Arduino UNO, NANO reserva por default -> SDA = A4 y SCL = A5 NANO
  //#define SCL 5 protocolo de comunicacion I2C The compiler will replace any mention of scl with the value 5 at compile time.
  //#define SDA 4 protocolo de comunicacion I2C The compiler will replace any mention of scl with the value 4 at compile time.
  Encoder myEnc(3,2);// PINES DIGITALES CON INTERRUPCION INVIERTE EL ORDEN INVIERTE SENTIDO DE lectura del GIRO
  #define boton 4 // BOTON DEL Encoder ROTATIVO
  #define pinFOTOPERIODO 11
  int inApin[2] = { 7, 4 }; // INA: Clockwise input sentido horario FRIO
  int inBpin[2] = { 8, 9 }; // INB: Counter-clockwise input sentido anti-horario CALOR
  int pwmpin[2] = { 5, 6 }; // PWM input
  //estos pines no estaran conectados
  int cspin[2] = { 2, 3 }; // CS: Current sense ANALOG input
  int enpin[2] = { 0, 1 }; // EN: Status of switches output (Analog pin)
  //int statpin = 13;// led onboard
  const int pinOPTOCUPLER = 9; // Led OPTOCUPLER cable verde de fuente
  const int pinPOTE = A3; // pote usar pin analog read MONITOREAR TENSION PUENTE H
  // PULSADORES SELECTORES
  pinMode(Sw3, INPUT); // pin ardu A1 pull down con resistencia 1K5 y FILTRO 100NF en PCB
  pinMode(Sw2, INPUT); // pin ardu A2 pull down con resistencia 1K5 y FILTRO 100NF en PCB
  pinMode(boton, INPUT_PULLUP); // pin del pulsador del Stepper rotatvo siempre UP
  pinMode(pinOPTOCUPLER, OUTPUT);
  pinMode(BUZZER, OUTPUT);
  pinMode(pinFOTOPERIODO, OUTPUT);
  EasyBuzzer.setPin(14);
  motorGo(0, 1, PwFrio);
  Voltimetro();
  ENTROPIA = "COOLING";
  //motorGo(motor, 1cool 2hot, pwm) pwm =0 a 1023
  // puente, F/C, pwm
  motorGo(0, 2, PwHot);
  Voltimetro();
  ENTROPIA = "HEATING"; //
  display oled 128*64 SSD1306
  1+ 10 +1 ancho caracter x2 =12
  4 12 4 borde caracteres borde =128
  -------------------------
  1+ 5 +1 ancho caracter x1 = 7
  1 18 1 borde caracteres borde =128
  coneciones:
  ONE_WIRE_BUS 12
  // 0X3C+SA0 - 0x3C or 0x3D
  #define I2C_ADDRESS 0x3C
  const int BUZZER = A0; //buzzer con led azul en paralelo usa pasivo con trNPN buffer rutina de tono 450Hz libreria easyBuzzer
  // protocolo de comunicacion I2C Arduino UNO, NANO reserva por default -> SDA = A4 y SCL = A5 NANO
  //#define SCL 5 protocolo de comunicacion I2C The compiler will replace any mention of scl with the value 5 at compile time.
  //#define SDA 4 protocolo de comunicacion I2C The compiler will replace any mention of scl with the value 4 at compile time.
  Encoder myEnc(3,2);// PINES DIGITALES CON INTERRUPCION INVIERTE EL ORDEN INVIERTE SENTIDO DE lectura del GIRO
  #define boton 4 // BOTON DEL Encoder ROTATIVO
  #define pinFOTOPERIODO 11
  int inApin[2] = { 7, 4 }; // INA: Clockwise input sentido horario FRIO
  int inBpin[2] = { 8, 9 }; // INB: Counter-clockwise input sentido anti-horario CALOR
  int pwmpin[2] = { 5, 6 }; // PWM input
  //estos pines no estaran conectados
  int cspin[2] = { 2, 3 }; // CS: Current sense ANALOG input
  int enpin[2] = { 0, 1 }; // EN: Status of switches output (Analog pin)
  //int statpin = 13;// led onboard
  const int pinOPTOCUPLER = 9; // Led OPTOCUPLER cable verde de fuente
  const int pinPOTE = A3; // pote usar pin analog read MONITOREAR TENSION PUENTE H
  // PULSADORES SELECTORES
  pinMode(Sw3, INPUT); // pin ardu A1 pull down con resistencia 1K5 y FILTRO 100NF en PCB
  pinMode(Sw2, INPUT); // pin ardu A2 pull down con resistencia 1K5 y FILTRO 100NF en PCB
  pinMode(boton, INPUT_PULLUP); // pin del pulsador del Stepper rotatvo siempre UP
  pinMode(pinOPTOCUPLER, OUTPUT);
  pinMode(BUZZER, OUTPUT);
  pinMode(pinFOTOPERIODO, OUTPUT);
  EasyBuzzer.setPin(14=A0);
  motorGo(0, 1, PwFrio);
  Voltimetro();
  ENTROPIA = "COOLING";
  //motorGo(motor, 1cool 2hot, pwm) pwm =0 a 1023
  // puente, F/C, pwm
  motorGo(0, 2, PwHot);
  Voltimetro();
  ENTROPIA = "HEATING"; //
  PUENTE-H 2
  3IN B a D4
  4IN B a D9
  5 PWM a D6
  enable 1 A0
  Led FUENTE ON
  Led ECO
  ON fuente
  eco
  PUENTE-H
  VNH 5019
  DOBLE
  GND
  +12v

custom parts:
  KY-040 Rotary encoder: KY-040 Rotary Encoder with switch on breakout borad from AZ Delivery
